// Logisim project 2.circ as structural Verilog: 1 circuit, main circuit main
module main (
  input  in_1,
  input  in_2,
  input  [1:0] in_3,
  input  Enable,
  output out_5
);

  wire and_1_out, nand_1_out, nor_1_out, or_1_out;

  and and_1 (and_1_out, in_2, in_1);
  or or_1 (or_1_out, in_2, in_1);
  nor nor_1 (nor_1_out, in_2, in_1);
  nand nand_1 (nand_1_out, in_2, in_1);
  Multiplexer #(.select(2)) multiplexer_1 (
    .in0(and_1_out), .in1(or_1_out), .in2(nor_1_out), .in3(nand_1_out), .out(out_5), .sel(in_3), .en(Enable));
endmodule
