// Logisim project 4.circ as structural Verilog: 1 circuit, main circuit main
module main (
  input  a,
  input  b,
  input  c,
  output x,
  output y,
  output z
);

  wire and_1_out, and_2_out, and_3_out, and_4_out, and_5_out, and_6_out, and_7_out, and_8_out, and_9_out,
       and_10_out, and_11_out, not_1_out, not_2_out, not_3_out, not_4_out, not_5_out, not_6_out, or_1_out,
       or_3_out, or_4_out;

  Hex_Digit_Display hex_digit_display_1 (.value({1'b0, a, b, c}));  // open: dp
  and and_1 (and_1_out, b, c);
  and and_2 (and_2_out, a, c);
  not not_1 (not_1_out, a);
  and and_3 (and_3_out, not_1_out, not_2_out);
  not not_2 (not_2_out, b);
  not not_3 (not_3_out, a);
  and and_4 (and_4_out, not_3_out, b);
  not not_4 (not_4_out, c);
  and and_5 (and_5_out, a, not_5_out);
  not not_5 (not_5_out, b);
  not not_6 (not_6_out, c);
  and and_6 (and_6_out, a, b);
  not not_7 (z, c);
  or or_1 (or_1_out, and_1_out, and_2_out);
  or or_2 (x, or_1_out, and_7_out);
  and and_7 (and_7_out, a, b);
  and and_8 (and_8_out, and_3_out, c);
  and and_9 (and_9_out, and_4_out, not_4_out);
  and and_10 (and_10_out, and_5_out, not_6_out);
  and and_11 (and_11_out, and_6_out, c);
  or or_3 (or_3_out, and_8_out, and_9_out);
  or or_4 (or_4_out, and_10_out, and_11_out);
  or or_5 (y, or_3_out, or_4_out);
  Hex_Digit_Display hex_digit_display_2 (.value({1'b0, x, y, z}));  // open: dp
endmodule
