// Logisim project 3.circ as structural Verilog: 3 circuits, main circuit main
module main (
  input  B3,
  input  A3,
  input  B2,
  input  A2,
  input  B1,
  input  A1,
  input  B0,
  input  A0,
  output Cout,
  output S3,
  output S2,
  output S1,
  output S0
);

  wire fulladder_2_cout, fulladder_3_cout, halfadder_1_cout;

  Hex_Digit_Display hex_digit_display_1 (.value({3'b000, Cout}));  // open: dp
  FullAdder fulladder_1 (.A(A3), .B(B3), .Cin(fulladder_2_cout), .S(S3), .Cout(Cout));
  Hex_Digit_Display hex_digit_display_2 (.value({B3, B2, B1, B0}));  // open: dp
  FullAdder fulladder_2 (.A(A2), .B(B2), .Cin(fulladder_3_cout), .S(S2), .Cout(fulladder_2_cout));
  Hex_Digit_Display hex_digit_display_3 (.value({A3, A2, A1, A0}));  // open: dp
  FullAdder fulladder_3 (.A(A1), .B(B1), .Cin(halfadder_1_cout), .S(S1), .Cout(fulladder_3_cout));
  HalfAdder halfadder_1 (.A(A0), .B(B0), .S(S0), .Cout(halfadder_1_cout));
  Hex_Digit_Display hex_digit_display_4 (.value({S3, S2, S1, S0}));  // open: dp
endmodule

module FullAdder (
  input  A,
  input  B,
  input  Cin,
  output S,
  output Cout
);

  wire and_1_out, and_2_out, xor_1_out;

  xor xor_1 (xor_1_out, A, B);
  and and_1 (and_1_out, Cin, xor_1_out);
  and and_2 (and_2_out, A, B);
  xor xor_2 (S, xor_1_out, Cin);
  or or_1 (Cout, and_1_out, and_2_out);
endmodule

module HalfAdder (
  input  A,
  input  B,
  output S,
  output Cout
);

  xor xor_1 (S, A, B);
  and and_1 (Cout, A, B);
endmodule
