// Logisim project 4.circ as structural Verilog: 2 circuits, main circuit main
module main (
  input  B3,
  input  A3,
  input  B2,
  input  A2,
  input  B1,
  input  A1,
  input  B0,
  input  A0,
  input  C0,
  output C4,
  output S3,
  output S2,
  output S1,
  output S0
);

  wire fulladder_2_cout, fulladder_3_cout, fulladder_4_cout, xor_1_out, xor_2_out, xor_3_out, xor_4_out;

  Hex_Digit_Display hex_digit_display_1 (.value({3'b000, C4}));  // open: dp
  xor xor_1 (xor_1_out, B3, C0);
  FullAdder fulladder_1 (.A(A3), .B(xor_1_out), .Cin(fulladder_2_cout), .S(S3), .Cout(C4));
  Hex_Digit_Display hex_digit_display_2 (.value({B3, B2, B1, B0}));  // open: dp
  xor xor_2 (xor_2_out, B2, C0);
  FullAdder fulladder_2 (.A(A2), .B(xor_2_out), .Cin(fulladder_3_cout), .S(S2), .Cout(fulladder_2_cout));
  xor xor_3 (xor_3_out, B1, C0);
  FullAdder fulladder_3 (.A(A1), .B(xor_3_out), .Cin(fulladder_4_cout), .S(S1), .Cout(fulladder_3_cout));
  Hex_Digit_Display hex_digit_display_3 (.value({A3, A2, A1, A0}));  // open: dp
  xor xor_4 (xor_4_out, B0, C0);
  FullAdder fulladder_4 (.A(A0), .B(xor_4_out), .Cin(C0), .S(S0), .Cout(fulladder_4_cout));
  Hex_Digit_Display hex_digit_display_4 (.value({3'b000, C0}));  // open: dp
  Hex_Digit_Display hex_digit_display_5 (.value({S3, S2, S1, S0}));  // open: dp
endmodule

module FullAdder (
  input  A,
  input  B,
  input  Cin,
  output S,
  output Cout
);

  wire and_1_out, and_2_out, xor_1_out;

  xor xor_1 (xor_1_out, A, B);
  and and_1 (and_1_out, Cin, xor_1_out);
  and and_2 (and_2_out, A, B);
  xor xor_2 (S, xor_1_out, Cin);
  or or_1 (Cout, and_1_out, and_2_out);
endmodule
