// Logisim project 1.circ as structural Verilog: 3 circuits, main circuit main
module main (
  input  S2,
  input  S1,
  input  S0,
  input  I0,
  input  I1,
  input  I2,
  input  I3,
  input  I4,
  input  I5,
  input  I6,
  input  I7,
  output Y
);

  wire n4_1_mux_1_o, n4_1_mux_2_o;

  _4_1_MUX u_4_1_mux_1 (.I0(I0), .I1(I1), .I2(I2), .I3(I3), .S1(S1), .S0(S0), .O(n4_1_mux_1_o));
  _4_1_MUX u_4_1_mux_2 (.I0(I4), .I1(I5), .I2(I6), .I3(I7), .S1(S1), .S0(S0), .O(n4_1_mux_2_o));
  _2_1_MUX u_2_1_mux_1 (.I0(n4_1_mux_1_o), .S(S2), .I1(n4_1_mux_2_o), .O(Y));
endmodule

module _2_1_MUX (
  input  I0,
  input  S,
  input  I1,
  output O
);

  wire and_1_out, and_2_out, not_1_out;

  not not_1 (not_1_out, S);
  and and_1 (and_1_out, I0, not_1_out);
  and and_2 (and_2_out, S, I1);
  or or_1 (O, and_1_out, and_2_out);
endmodule

module _4_1_MUX (
  input  S1,
  input  S0,
  input  I0,
  input  I1,
  input  I2,
  input  I3,
  output O
);

  wire and_1_out, and_2_out, and_3_out, and_4_out, not_1_out, not_2_out;

  not not_1 (not_1_out, S1);
  not not_2 (not_2_out, S0);
  and and_1 (and_1_out, not_1_out, not_2_out, I0);
  and and_2 (and_2_out, not_1_out, S0, I1);
  and and_3 (and_3_out, S1, not_2_out, I2);
  and and_4 (and_4_out, S1, S0, I3);
  or or_1 (O, and_1_out, and_2_out, and_3_out, and_4_out);
endmodule
