// Logisim project 2.circ as structural Verilog: 2 circuits, main circuit main
module main (
  input  S2,
  input  S1,
  input  S0,
  input  INPUT,
  output O0,
  output O1,
  output O2,
  output O3,
  output O4,
  output O5,
  output O6,
  output O7
);

  wire n1_4_demux_1_i0, n1_4_demux_1_i2;

  _1_4_DEMUX u_1_4_demux_1 (.D(INPUT), .I0(n1_4_demux_1_i0), .I2(n1_4_demux_1_i2), .S0(1'b0), .S1(S2));  // open: I1, I3
  _1_4_DEMUX u_1_4_demux_2 (.D(n1_4_demux_1_i0), .I0(O0), .I1(O1), .I2(O2), .I3(O3), .S0(S0), .S1(S1));
  _1_4_DEMUX u_1_4_demux_3 (.D(n1_4_demux_1_i2), .I0(O4), .I1(O5), .I2(O6), .I3(O7), .S0(S0), .S1(S1));
endmodule

module _1_4_DEMUX (
  input  S0,
  input  S1,
  input  D,
  output I0,
  output I1,
  output I2,
  output I3
);

  wire not_1_out, not_2_out;

  not not_1 (not_1_out, S0);
  not not_2 (not_2_out, S1);
  and and_1 (I0, not_1_out, not_2_out, D);
  and and_2 (I1, not_2_out, S0, D);
  and and_3 (I2, not_1_out, S1, D);
  and and_4 (I3, S0, S1, D);
endmodule
