// Logisim project 3.circ as structural Verilog: 1 circuit, main circuit main
module main (
  input  D3,
  input  D2,
  input  D1,
  input  D0,
  output Q1_D2_D3,
  output Q0_D1_D3
);

  _7_Segment_Display u_7_segment_display_1 (.g(D3), .a(D3), .b(D3), .d(D3), .c(D3));  // open: f, e, dp
  _7_Segment_Display u_7_segment_display_2 (.g(D2), .a(D2), .b(D2), .e(D2), .d(D2));  // open: f, c, dp
  _7_Segment_Display u_7_segment_display_3 (.b(D1), .c(D1));  // open: g, f, a, e, d, dp
  _7_Segment_Display u_7_segment_display_4 (.f(D0), .a(D0), .b(D0), .e(D0), .d(D0), .c(D0));  // open: g, dp
  or or_1 (Q1_D2_D3, D2, D3);
  or or_2 (Q0_D1_D3, D1, D3);
  Hex_Digit_Display hex_digit_display_1 (.value({3'b000, Q1_D2_D3}));  // open: dp
  Hex_Digit_Display hex_digit_display_2 (.value({3'b000, Q0_D1_D3}));  // open: dp
endmodule
