// Logisim project 4.circ as structural Verilog: 2 circuits, main circuit main
module main (
  input  A0,
  input  A1,
  input  A2_E,
  output I0,
  output I1,
  output I2,
  output I3,
  output I4,
  output I5,
  output I6,
  output I7
);

  wire not_1_out;

  _2_to_4_Decoder u_2_to_4_decoder_1 (.A1(A1), .A0(A0), .Enable(not_1_out), .Y3(I3), .Y2(I2), .Y1(I1), .Y0(I0));
  not not_1 (not_1_out, A2_E);
  _2_to_4_Decoder u_2_to_4_decoder_2 (.A1(A1), .A0(A0), .Enable(A2_E), .Y3(I7), .Y2(I6), .Y1(I5), .Y0(I4));
endmodule

module _2_to_4_Decoder (
  input  A1,
  input  A0,
  input  Enable,
  output Y3,
  output Y2,
  output Y1,
  output Y0
);

  wire not_1_out, not_2_out;

  not not_1 (not_1_out, A1);
  not not_2 (not_2_out, A0);
  and and_1 (Y3, A1, A0, Enable);
  and and_2 (Y2, A1, not_2_out, Enable);
  and and_3 (Y1, not_1_out, A0, Enable);
  and and_4 (Y0, not_1_out, not_2_out, Enable);
endmodule
