// Logisim project q2.circ as structural Verilog: 1 circuit, main circuit main
module main (
  input  _0,
  input  _1,
  input  _2,
  input  _3,
  input  _4,
  input  _5,
  input  _6,
  input  _7
);

  wire and_1_out, and_2_out, and_3_out, and_4_out, and_5_out, not_1_out, not_2_out, not_3_out, or_1_out,
       or_2_out, or_3_out, priority_encoder_1_gs;
  wire [2:0] priority_encoder_1_out;

  Hex_Digit_Display hex_digit_display_1 (.value({1'b0, priority_encoder_1_out}));  // open: dp
  Priority_Encoder priority_encoder_1 (
    .in0(_0), .in1(_1), .in2(_2), .in3(_3), .in4(_4), .in5(_5), .in6(_6), .in7(_7),
    .out(priority_encoder_1_out), .gs(priority_encoder_1_gs));  // open: en_in, en_out
  and and_1 (and_1_out, priority_encoder_1_out[2], priority_encoder_1_out[0]);
  and and_2 (and_2_out, priority_encoder_1_out[1], not_1_out);
  not not_1 (not_1_out, priority_encoder_1_out[2]);
  _7_Segment_Display u_7_segment_display_1 (
    .g(or_1_out), .f(and_5_out), .a(and_5_out), .b(or_3_out), .e(and_5_out), .d(and_4_out), .c(and_3_out));  // open: dp
  or or_1 (or_1_out, not_2_out, or_2_out);
  not not_2 (not_2_out, priority_encoder_1_out[0]);
  or or_2 (or_2_out, and_1_out, and_2_out);
  or or_3 (or_3_out, or_2_out, priority_encoder_1_out[0]);
  and and_3 (and_3_out, priority_encoder_1_out[0], not_3_out);
  not not_3 (not_3_out, or_2_out);
  and and_4 (and_4_out, 1'b1, not_3_out);
  and and_5 (and_5_out, 1'b1, priority_encoder_1_gs);
endmodule
