// Logisim project q3.circ as structural Verilog: 1 circuit, main circuit main
module main (
  input  Jan,
  input  Feb,
  input  Mar,
  input  Apr,
  input  May,
  input  Jun,
  input  July,
  input  Aug,
  input  Sept,
  input  Oct,
  input  Nov,
  input  Dec,
  input  Leap
);

  wire and_1_out, and_2_out, and_3_out, and_4_out, and_5_out, and_6_out, not_1_out, not_2_out, not_3_out,
       not_4_out, not_5_out, or_1_out, or_2_out, or_3_out, priority_encoder_1_gs;
  wire [3:0] priority_encoder_1_out;

  Hex_Digit_Display hex_digit_display_1 (.value(priority_encoder_1_out));  // open: dp
  Priority_Encoder #(.select(4)) priority_encoder_1 (
    .in0(1'b0), .in1(Jan), .in2(Feb), .in3(Mar), .in4(Apr), .in5(May), .in6(Jun), .in7(July), .in8(Aug),
    .in9(Sept), .in10(Oct), .in11(Nov), .in12(Dec), .in13(1'b0), .in14(1'b0), .in15(1'b0),
    .out(priority_encoder_1_out), .gs(priority_encoder_1_gs));  // open: en_out, en_in
  not not_1 (not_1_out, priority_encoder_1_out[0]);
  not not_2 (not_2_out, priority_encoder_1_out[2]);
  not not_3 (not_3_out, priority_encoder_1_out[3]);
  _7_Segment_Display u_7_segment_display_1 (
    .g(and_2_out), .a(and_2_out), .b(and_2_out), .e(and_1_out), .d(and_2_out), .c(not_4_out));  // open: f, dp
  not not_4 (not_4_out, and_1_out);
  and and_1 (and_1_out, not_1_out, priority_encoder_1_out[1], not_2_out, not_3_out);
  and and_2 (and_2_out, 1'b1, priority_encoder_1_gs);
  not not_5 (not_5_out, Leap);
  _7_Segment_Display u_7_segment_display_2 (
    .g(and_4_out), .f(or_2_out), .a(or_2_out), .b(and_2_out), .e(or_1_out), .d(or_2_out), .c(and_2_out));  // open: dp
  or or_1 (or_1_out, and_3_out, or_3_out);
  and and_3 (and_3_out, not_5_out, and_4_out);
  and and_4 (and_4_out, and_1_out, 1'b1);
  and and_5 (and_5_out, not_1_out, priority_encoder_1_out[2], not_3_out);
  and and_6 (and_6_out, priority_encoder_1_out[0], priority_encoder_1_out[3]);
  or or_2 (or_2_out, or_3_out, and_4_out);
  or or_3 (or_3_out, and_5_out, and_6_out);
endmodule
