// Logisim project q4.circ as structural Verilog: 1 circuit, main circuit main
module main (
  input  Yo,
  input  Yo_2,
  input  Yo_3,
  input  Yo_4,
  input  Yt0,
  input  Yt1,
  input  Yt2,
  input  Yt3,
  input  Yh0,
  input  Yh1,
  input  Yh2,
  input  Yh3,
  input  Yth0,
  input  Yth1,
  input  Yth2,
  input  Yth3,
  output Leap
);

  wire and_1_out, and_2_out, and_3_out, and_4_out, and_5_out, and_6_out, and_7_out, not_1_out, not_2_out,
       not_3_out, not_4_out, not_5_out, not_6_out, not_7_out, not_8_out, not_9_out, or_1_out, or_2_out;

  not not_1 (not_1_out, Yo);
  not not_2 (not_2_out, Yo_2);
  not not_3 (not_3_out, Yo_3);
  not not_4 (not_4_out, Yo_4);
  not not_5 (not_5_out, Yt0);
  not not_6 (not_6_out, Yt1);
  not not_7 (not_7_out, Yt2);
  not not_8 (not_8_out, Yt3);
  and and_1 (and_1_out, ~Yh0, ~Yh1, ~Yth0);  // AND_Gate
  and and_2 (and_2_out, Yth0, Yh1, ~Yh0);  // AND_Gate
  and and_3 (and_3_out, not_1_out, Yo_2, Yt0);
  and and_4 (and_4_out, not_1_out, not_2_out, not_5_out);
  or or_1 (or_1_out, and_1_out, and_2_out);
  or or_2 (or_2_out, and_3_out, and_4_out);
  and and_5 (and_5_out, not_1_out, not_2_out, not_3_out, not_4_out, not_5_out, not_6_out, not_7_out, not_8_out);
  and and_6 (and_6_out, or_2_out, not_9_out);
  not not_9 (not_9_out, and_5_out);
  and and_7 (and_7_out, and_5_out, or_1_out);
  or or_3 (Leap, and_6_out, and_7_out);
endmodule
