// Logisim project Q1.circ as structural Verilog: 1 circuit, main circuit main
module main (
  input  in_1,
  input  in_2,
  input  [3:0] A,
  input  [3:0] B,
  input  [3:0] C,
  input  [3:0] D,
  output [3:0] F
);

  Multiplexer #(.select(2)) multiplexer_1 (
    .in0(A[3]), .in1(B[3]), .in2(C[3]), .in3(D[3]), .out(F[3]), .sel({in_1, in_2}));  // open: en
  Multiplexer #(.select(2)) multiplexer_2 (
    .in0(A[2]), .in1(B[2]), .in2(C[2]), .in3(D[2]), .out(F[2]), .sel({in_1, in_2}));  // open: en
  Multiplexer #(.select(2)) multiplexer_3 (
    .in0(A[1]), .in1(B[1]), .in2(C[1]), .in3(D[1]), .out(F[1]), .sel({in_1, in_2}));  // open: en
  Multiplexer #(.select(2)) multiplexer_4 (
    .in0(A[0]), .in1(B[0]), .in2(C[0]), .in3(D[0]), .out(F[0]), .sel({in_1, in_2}));  // open: en
endmodule
