// Logisim project Q2.circ as structural Verilog: 1 circuit, main circuit main
module main (
  input  [3:0] A,
  input  S1,
  input  S0,
  input  [3:0] B,
  input  [3:0] C,
  input  [3:0] D,
  output [3:0] F
);

  wire decoder_1_out0, decoder_1_out1, decoder_1_out2, decoder_1_out3;

  Decoder #(.select(2)) decoder_1 (
    .out0(decoder_1_out0), .out1(decoder_1_out1), .out2(decoder_1_out2), .out3(decoder_1_out3), .sel({S1, S0}));  // open: en
  assign F[0] = decoder_1_out0 ? A[0] : 1'bz;  // Controlled_Buffer controlled_buffer_1
  assign F[1] = decoder_1_out0 ? A[1] : 1'bz;  // Controlled_Buffer controlled_buffer_2
  assign F[2] = decoder_1_out0 ? A[2] : 1'bz;  // Controlled_Buffer controlled_buffer_3
  assign F[3] = decoder_1_out0 ? A[3] : 1'bz;  // Controlled_Buffer controlled_buffer_4
  assign F[0] = decoder_1_out1 ? B[0] : 1'bz;  // Controlled_Buffer controlled_buffer_5
  assign F[1] = decoder_1_out1 ? B[1] : 1'bz;  // Controlled_Buffer controlled_buffer_6
  assign F[2] = decoder_1_out1 ? B[2] : 1'bz;  // Controlled_Buffer controlled_buffer_7
  assign F[3] = decoder_1_out1 ? B[3] : 1'bz;  // Controlled_Buffer controlled_buffer_8
  assign F[0] = decoder_1_out2 ? C[0] : 1'bz;  // Controlled_Buffer controlled_buffer_9
  assign F[1] = decoder_1_out2 ? C[1] : 1'bz;  // Controlled_Buffer controlled_buffer_10
  assign F[2] = decoder_1_out2 ? C[2] : 1'bz;  // Controlled_Buffer controlled_buffer_11
  assign F[3] = decoder_1_out2 ? C[3] : 1'bz;  // Controlled_Buffer controlled_buffer_12
  assign F[0] = decoder_1_out3 ? D[0] : 1'bz;  // Controlled_Buffer controlled_buffer_13
  assign F[1] = decoder_1_out3 ? D[1] : 1'bz;  // Controlled_Buffer controlled_buffer_14
  assign F[2] = decoder_1_out3 ? D[2] : 1'bz;  // Controlled_Buffer controlled_buffer_15
  assign F[3] = decoder_1_out3 ? D[3] : 1'bz;  // Controlled_Buffer controlled_buffer_16
endmodule
