// Logisim project Q4.circ as structural Verilog: 1 circuit, main circuit main
module main (
  input  [3:0] A,
  input  [3:0] B,
  input  [1:0] SL,
  output [3:0] F
);

  Multiplexer #(.select(2), .width(4)) multiplexer_1 (
    .in0({A[2:0], 1'b0}), .in1({B[0], B[3:1]}), .in2({{2{A[3]}}, A[2:1]}), .in3({B[0], B[2:1], B[3]}),
    .out(F), .sel(SL));  // open: en
endmodule
