// Logisim project Q1.circ as structural Verilog: 2 circuits, main circuit main
module main (
  input  [3:0] A,
  input  [3:0] B,
  input  S0,
  input  S1,
  input  S2,
  output [3:0] out_6
);

  wire [3:0] alu_1_out_4, and_1_out, multiplexer_1_out, multiplexer_2_out, multiplexer_3_out, shifter_1_out,
       shifter_2_out, xor_1_out;

  assign and_1_out = A & B;  // AND_Gate and_1, 4 bits wide
  Shifter #(.width(4), .shift("rl")) shifter_1 (.in(A), .\dist (2'b01), .out(shifter_1_out));
  Shifter #(.width(4), .shift("ar")) shifter_2 (.in(B), .\dist (2'b01), .out(shifter_2_out));
  ALU alu_1 (.A(A), .B(B), .in_3({S1, S0}), .out_4(alu_1_out_4));
  assign xor_1_out = A ^ B;  // XOR_Gate xor_1, 4 bits wide
  Multiplexer #(.width(4)) multiplexer_1 (
    .in0(xor_1_out), .in1(and_1_out), .out(multiplexer_1_out), .sel(S0));  // open: en
  Multiplexer #(.width(4)) multiplexer_2 (
    .in0(shifter_1_out), .in1(shifter_2_out), .out(multiplexer_2_out), .sel(S0));  // open: en
  Multiplexer #(.width(4)) multiplexer_3 (
    .in0(multiplexer_1_out), .in1(multiplexer_2_out), .out(multiplexer_3_out), .sel(S1));  // open: en
  Multiplexer #(.width(4)) multiplexer_4 (
    .in0(alu_1_out_4), .in1(multiplexer_3_out), .out(out_6), .sel(S2));  // open: en
endmodule

module ALU (
  input  [3:0] A,
  input  [3:0] B,
  input  [1:0] in_3,
  output [3:0] out_4
);

  wire [3:0] adder_1_out, subtractor_1_out, subtractor_2_out;

  Subtractor #(.width(4)) subtractor_1 (.a(A), .b(B), .out(subtractor_1_out));  // open: bin, bout
  Adder #(.width(4)) adder_1 (.a(A), .b(B), .out(adder_1_out));  // open: cin, cout
  Subtractor #(.width(4)) subtractor_2 (.a(A), .b(4'b0101), .out(subtractor_2_out));  // open: bin, bout
  Multiplexer #(.select(2), .width(4)) multiplexer_1 (
    .in0(A), .in1(subtractor_1_out), .in2(adder_1_out), .in3(subtractor_2_out), .out(out_4), .sel(in_3));  // open: en
endmodule
