// Logisim project All-in-One logic gate circuit 1 bit.circ as structural Verilog: 1 circuit, main circuit main
module main (
  input  A,
  input  B,
  output C,
  output D,
  output E,
  output F,
  output G
);

  not not_1 (C, A);
  and and_1 (D, A, B);
  or or_1 (E, A, B);
  nand nand_1 (F, A, B);
  xor xor_1 (G, A, B);

  // Notes on the sheet:
  //   All in one logic circuit
  //   Soham Ghosh
  //   231B341
endmodule
