// Logisim project All-in-One logic gate circuit 4 bit.circ as structural Verilog: 1 circuit, main circuit main
module main (
  input  [3:0] A,
  input  [3:0] B,
  output [3:0] C,
  output [3:0] D,
  output [3:0] E,
  output [3:0] F,
  output [3:0] G
);

  assign C = ~A;  // NOT_Gate not_1, 4 bits wide
  assign D = A & B;  // AND_Gate and_1, 4 bits wide
  assign E = A | B;  // OR_Gate or_1, 4 bits wide
  assign F = ~(A & B);  // NAND_Gate nand_1, 4 bits wide
  assign G = A ^ B;  // XOR_Gate xor_1, 4 bits wide

  // Notes on the sheet:
  //   4 bit All in one logic circuit
  //   Soham Ghosh
  //   231b341
endmodule
