// Logisim project Q2 8 data width.circ as structural Verilog: 1 circuit, main circuit main
module main (
  input  [7:0] X,
  input  [7:0] Y,
  input  [7:0] A,
  input  [7:0] B,
  output [7:0] O
);

  wire [7:0] and_1_out, and_2_out, and_3_out, not_1_out, not_2_out, not_3_out, xor_1_out;

  assign not_1_out = ~Y;  // NOT_Gate not_1, 8 bits wide
  assign not_2_out = ~A;  // NOT_Gate not_2, 8 bits wide
  assign not_3_out = ~B;  // NOT_Gate not_3, 8 bits wide
  assign and_1_out = not_3_out & not_2_out & Y;  // AND_Gate and_1, 8 bits wide
  assign and_2_out = A & B & not_1_out;  // AND_Gate and_2, 8 bits wide
  assign xor_1_out = A ^ B;  // XOR_Gate xor_1, 8 bits wide
  assign and_3_out = xor_1_out & X;  // AND_Gate and_3, 8 bits wide
  assign O = and_1_out | and_2_out | and_3_out;  // OR_Gate or_1, 8 bits wide

  // Notes on the sheet:
  //   All in one logic gate 8 data width
  //   Soham Ghosh
  //   231b341
endmodule
