// Logisim project Q2.circ as structural Verilog: 1 circuit, main circuit main
module main (
  input  X,
  input  Y,
  input  A,
  input  B,
  output O
);

  wire and_1_out, and_2_out, and_3_out, not_1_out, not_2_out, not_3_out, xor_1_out;

  not not_1 (not_1_out, A);
  not not_2 (not_2_out, Y);
  not not_3 (not_3_out, B);
  and and_1 (and_1_out, not_1_out, not_3_out, Y);
  and and_2 (and_2_out, A, B, not_2_out);
  xor xor_1 (xor_1_out, A, B);
  or or_1 (O, and_1_out, and_2_out, and_3_out);
  and and_3 (and_3_out, xor_1_out, X);

  // Notes on the sheet:
  //   All in one logic gate
  //   Soham Ghosh
  //   231b341
endmodule
