// Logisim project q3.circ as structural Verilog: 1 circuit, main circuit main
module main (
  input  A,
  input  B,
  input  C,
  output O
);

  wire and_1_out, and_2_out, and_3_out;

  and and_1 (and_1_out, B, C);
  or or_1 (O, and_1_out, and_2_out, and_3_out);
  and and_2 (and_2_out, A, C);
  and and_3 (and_3_out, A, B);

  // Notes on the sheet:
  //   Majority Detector
  //   Soham Ghosh
  //   231b341
endmodule
