// Logisim project Q4.circ as structural Verilog: 1 circuit, main circuit main
module main (
  input  IO,
  input  I1,
  input  I2,
  output O0,
  output O1,
  output O2
);

  wire and_1_out, and_2_out, and_3_out, and_4_out, and_5_out, and_6_out, and_7_out, not_1_out, not_2_out;

  Hex_Digit_Display hex_digit_display_1 (.value({1'b0, IO, I1, I2}));  // open: dp
  not not_1 (not_1_out, IO);
  not not_2 (not_2_out, I1);
  not not_3 (O2, I2);
  and and_1 (and_1_out, I1, I2);
  and and_2 (and_2_out, IO, I1);
  and and_3 (and_3_out, IO, I2);
  and and_4 (and_4_out, not_1_out, not_2_out, I2);
  and and_5 (and_5_out, IO, not_2_out, O2);
  and and_6 (and_6_out, IO, I1, I2);
  and and_7 (and_7_out, not_1_out, I1, O2);
  or or_1 (O0, and_1_out, and_2_out, and_3_out);
  or or_2 (O1, and_4_out, and_5_out, and_6_out, and_7_out);
  Hex_Digit_Display hex_digit_display_2 (.value({1'b0, O0, O1, O2}));  // open: dp

  // Notes on the sheet:
  //   Incrementer and Decrementer
  //   Soham Ghosh
  //   231b341
endmodule
