// Logisim project q1 full adder.circ as structural Verilog: 5 circuits, main circuit Half Adder
module Half_Adder (
  input  A,
  input  B,
  output Sum,
  output Carry
);

  xor xor_1 (Sum, B, A);
  and and_1 (Carry, B, A);

  // Notes on the sheet:
  //   Half Adder
  //   Soham Ghosh
  //   231b341
endmodule

module full_adder (
  input  A,
  input  B,
  input  C,
  output SUM,
  output Carry
);

  wire half_adder_1_carry, half_adder_1_sum, half_adder_2_carry;

  Half_Adder half_adder_1 (.Sum(half_adder_1_sum), .Carry(half_adder_1_carry), .A(A), .B(B));
  Half_Adder half_adder_2 (.Sum(SUM), .Carry(half_adder_2_carry), .A(half_adder_1_sum), .B(C));
  or or_1 (Carry, half_adder_2_carry, half_adder_1_carry);

  // Notes on the sheet:
  //   Full Adder
  //   Soham Ghosh
  //   231b341
endmodule

module _4bit_adder (
  input  B3,
  input  A3,
  input  B2,
  input  A2,
  input  B1,
  input  A1,
  input  B0,
  input  A0,
  output C4,
  output S3,
  output S2,
  output S1,
  output S0
);

  wire FA_1_carry, FA_2_carry, HA_carry;

  Hex_Digit_Display hex_digit_display_1 (.value({B3, B2, B1, B0}));  // open: dp
  Hex_Digit_Display hex_digit_display_2 (.value({S3, S2, S1, S0}));  // open: dp
  Hex_Digit_Display hex_digit_display_3 (.value({3'b000, C4}));  // open: dp
  full_adder FA_3 (.A(A3), .B(B3), .SUM(S3), .C(FA_2_carry), .Carry(C4));
  full_adder FA_2 (.A(A2), .B(B2), .SUM(S2), .C(FA_1_carry), .Carry(FA_2_carry));
  full_adder FA_1 (.A(A1), .B(B1), .SUM(S1), .C(HA_carry), .Carry(FA_1_carry));
  Half_Adder HA (.Sum(S0), .Carry(HA_carry), .A(A0), .B(B0));
  Hex_Digit_Display hex_digit_display_4 (.value({A3, A2, A1, A0}));  // open: dp

  // Notes on the sheet:
  //   4 bit Ripple Adder
  //   Soham Ghosh
  //   231b341
endmodule

module _4_bit_adder_subtracter (
  input  B3,
  input  A3,
  input  B2,
  input  A2,
  input  B1,
  input  A1,
  input  B0,
  input  A0,
  input  C0,
  output C4,
  output S3,
  output S2,
  output S1,
  output S0
);

  wire FA_1_carry, FA_2_carry, FA_3_carry, xor_1_out, xor_2_out, xor_3_out, xor_4_out;

  Hex_Digit_Display hex_digit_display_1 (.value({B3, B2, B1, B0}));  // open: dp
  Hex_Digit_Display hex_digit_display_2 (.value({3'b000, C4}));  // open: dp
  Hex_Digit_Display hex_digit_display_3 (.value({S3, S2, S1, S0}));  // open: dp
  xor xor_1 (xor_1_out, B3, C0);
  full_adder FA_4 (.A(A3), .B(xor_1_out), .SUM(S3), .C(FA_3_carry), .Carry(C4));
  xor xor_2 (xor_2_out, B1, C0);
  xor xor_3 (xor_3_out, B2, C0);
  full_adder FA_2 (.A(A1), .B(xor_2_out), .SUM(S1), .C(FA_1_carry), .Carry(FA_2_carry));
  full_adder FA_3 (.A(A2), .B(xor_3_out), .SUM(S2), .C(FA_2_carry), .Carry(FA_3_carry));
  xor xor_4 (xor_4_out, B0, C0);
  full_adder FA_1 (.A(A0), .B(xor_4_out), .SUM(S0), .C(C0), .Carry(FA_1_carry));
  Hex_Digit_Display hex_digit_display_4 (.value({A3, A2, A1, A0}));  // open: dp

  // Notes on the sheet:
  //   4 bit Adder/Subtractor
  //   231b341
  //   Soham Ghosh
endmodule

module FULL_ADDER_LOGIC_GATES (
  input  A,
  input  B,
  input  C,
  output SUM,
  output CARRY
);

  wire and_1_out, and_2_out, xor_1_out;

  xor xor_1 (xor_1_out, A, B);
  and and_1 (and_1_out, A, B);
  xor xor_2 (SUM, xor_1_out, C);
  and and_2 (and_2_out, C, xor_1_out);
  or or_1 (CARRY, and_2_out, and_1_out);

  // Notes on the sheet:
  //   Full Adder
  //   Soham Ghosh
  //   231b341
endmodule
