// Logisim project q1 half subtracter.circ as structural Verilog: 1 circuit, main circuit Half Substracter
// hs1
module Half_Substracter (
  input  A,
  input  B,
  output Difference,
  output Borrow
);

  wire not_1_out;

  not not_1 (not_1_out, A);
  xor xor_1 (Difference, B, A);
  and and_1 (Borrow, B, not_1_out);

  // Notes on the sheet:
  //   Half Subtractor
  //   Soham Ghosh
  //   231b341
endmodule
