// Logisim project Q1.circ as structural Verilog: 3 circuits, main circuit 2*1 MUX
module _2_1_MUX (
  input  B,
  input  S0,
  input  A,
  output O
);

  wire and_1_out, and_2_out, not_1_out;

  not not_1 (not_1_out, S0);
  and and_1 (and_1_out, A, not_1_out);
  and and_2 (and_2_out, S0, B);
  or or_1 (O, and_1_out, and_2_out);
endmodule

module _4_2_MUX (
  input  S0,
  input  A,
  input  B,
  input  C,
  input  D,
  input  S1,
  output O
);

  wire n2_1_mux_1_o, n2_1_mux_2_o;

  _2_1_MUX u_2_1_mux_1 (.O(n2_1_mux_1_o), .B(B), .S0(S0), .A(A));
  _2_1_MUX u_2_1_mux_2 (.O(n2_1_mux_2_o), .B(D), .S0(S0), .A(C));
  _2_1_MUX u_2_1_mux_3 (.O(O), .B(n2_1_mux_2_o), .S0(S1), .A(n2_1_mux_1_o));
endmodule

module _8_2_MUX (
  input  S0,
  input  S1,
  input  A,
  input  B,
  input  C,
  input  D,
  input  E,
  input  F,
  input  S2,
  input  G,
  input  H,
  output O
);

  wire n4_2_mux_1_o, n4_2_mux_2_o;

  _4_2_MUX u_4_2_mux_1 (.A(A), .B(B), .C(C), .D(D), .S0(S0), .S1(S1), .O(n4_2_mux_1_o));
  _4_2_MUX u_4_2_mux_2 (.A(E), .B(F), .C(G), .D(H), .S0(S0), .S1(S1), .O(n4_2_mux_2_o));
  _2_1_MUX u_2_1_mux_1 (.O(O), .B(n4_2_mux_2_o), .S0(S2), .A(n4_2_mux_1_o));
endmodule
