// Logisim project Q2.circ as structural Verilog: 3 circuits, main circuit 1*2
module _1_2 (
  input  S0,
  input  A,
  output O1,
  output O2
);

  wire not_1_out;

  not not_1 (not_1_out, S0);
  and and_1 (O1, not_1_out, A);
  and and_2 (O2, A, S0);
endmodule

module _1_4 (
  input  S1,
  input  S0,
  input  A,
  output O0,
  output O1,
  output O2,
  output O3
);

  wire n1_2_2_o1, n1_2_2_o2;

  _1_2 u_1_2_1 (.A(n1_2_2_o1), .S0(S1), .O1(O0), .O2(O1));
  _1_2 u_1_2_2 (.A(A), .S0(S0), .O1(n1_2_2_o1), .O2(n1_2_2_o2));
  _1_2 u_1_2_3 (.A(n1_2_2_o2), .S0(S1), .O1(O2), .O2(O3));
endmodule

module _1_8 (
  input  S2,
  input  S1,
  input  S0,
  input  A,
  output O0,
  output O1,
  output O2,
  output O3,
  output O4,
  output O5,
  output O6,
  output O7
);

  wire n1_4_1_o0, n1_4_1_o1;

  _1_4 u_1_4_1 (.A(A), .S1(S2), .S0(1'b0), .O0(n1_4_1_o0), .O1(n1_4_1_o1));  // open: O2, O3
  _1_4 u_1_4_2 (.A(n1_4_1_o0), .S1(S0), .S0(S1), .O0(O0), .O1(O1), .O2(O2), .O3(O3));
  _1_4 u_1_4_3 (.A(n1_4_1_o1), .S1(S0), .S0(S1), .O0(O4), .O1(O5), .O2(O6), .O3(O7));
endmodule
