// Logisim project Q3.circ as structural Verilog: 1 circuit, main circuit 4*2 ENC
// 4
module _4_2_ENC (
  input  I0,
  input  I1,
  input  I2,
  input  I3,
  output O0,
  output O1
);

  _7_Segment_Display u_7_segment_display_1 (.f(I0), .a(I0), .b(I0), .e(I0), .d(I0), .c(I0));  // open: g, dp
  _7_Segment_Display u_7_segment_display_2 (.b(I1), .c(I1));  // open: g, f, a, e, d, dp
  _7_Segment_Display u_7_segment_display_3 (.g(I2), .a(I2), .b(I2), .e(I2), .d(I2));  // open: f, c, dp
  _7_Segment_Display u_7_segment_display_4 (.g(I3), .a(I3), .b(I3), .d(I3), .c(I3));  // open: f, e, dp
  or or_1 (O0, I1, I3);
  or or_2 (O1, I2, I3);
  Hex_Digit_Display hex_digit_display_1 (.value({3'b000, O1}));  // open: dp
  Hex_Digit_Display hex_digit_display_2 (.value({3'b000, O0}));  // open: dp
endmodule
