// Logisim project Q4.circ as structural Verilog: 2 circuits, main circuit 2*4 DEC
module _2_4_DEC (
  input  EN,
  input  A1,
  input  A0,
  output O0,
  output O1,
  output O2,
  output O3
);

  wire not_1_out, not_2_out;

  not not_1 (not_1_out, A1);
  not not_2 (not_2_out, A0);
  and and_1 (O0, not_2_out, EN, not_1_out);
  and and_2 (O1, A0, EN, not_1_out);
  and and_3 (O2, not_2_out, EN, A1);
  and and_4 (O3, A0, EN, A1);
endmodule

module _3_8_DEC (
  input  A0,
  input  A1,
  input  A3,
  output O0,
  output O1,
  output O2,
  output O3,
  output O4,
  output O5,
  output O6,
  output O7_prime
);

  wire not_1_out;

  not not_1 (not_1_out, A3);
  _2_4_DEC u_2_4_dec_1 (.O0(O0), .O1(O1), .O2(O2), .O3(O3), .A1(A1), .A0(A0), .EN(not_1_out));
  _2_4_DEC u_2_4_dec_2 (.O0(O4), .O1(O5), .O2(O6), .O3(O7_prime), .A1(A1), .A0(A0), .EN(A3));
endmodule
