// Logisim project q1.circ as structural Verilog: 2 circuits, main circuit Full Adder4:1
module Full_Adder4_1 (
  input  A,
  input  B,
  input  C,
  output Sum,
  output Carry
);

  wire not_1_out;

  not not_1 (not_1_out, C);
  Multiplexer #(.select(2), .enable("false")) multiplexer_1 (
    .in0(C), .in1(not_1_out), .in2(not_1_out), .in3(C), .out(Sum), .sel({B, A}));
  Multiplexer #(.select(2), .enable("false")) multiplexer_2 (
    .in0(1'b0), .in1(C), .in2(C), .in3(1'b1), .out(Carry), .sel({B, A}));
endmodule

module Full_Adder_8_1 (
  input  A,
  input  B,
  input  C,
  output Sum,
  output Carry
);

  Multiplexer #(.select(3), .enable("false")) multiplexer_1 (
    .in0(1'b0), .in1(1'b1), .in2(1'b1), .in3(1'b0), .in4(1'b1), .in5(1'b0), .in6(1'b0), .in7(1'b1),
    .out(Sum), .sel({C, B, A}));
  Multiplexer #(.select(3), .enable("false")) multiplexer_2 (
    .in0(1'b0), .in1(1'b0), .in2(1'b0), .in3(1'b1), .in4(1'b0), .in5(1'b1), .in6(1'b1), .in7(1'b1),
    .out(Carry), .sel({C, B, A}));
endmodule
