// Logisim project Q2.circ as structural Verilog: 1 circuit, main circuit main
module main (
  input  A0,
  input  A1,
  input  B0,
  input  B1,
  output X0,
  output X1,
  output X2,
  output X3
);

  wire adder_1_cout, and_2_out, and_3_out, and_4_out;

  Hex_Digit_Display hex_digit_display_1 (.value({2'b00, B1, B0}));  // open: dp
  Hex_Digit_Display hex_digit_display_2 (.value({2'b00, A1, A0}));  // open: dp
  and and_1 (X0, A0, B0);
  and and_2 (and_2_out, A1, B0);
  and and_3 (and_3_out, A0, B1);
  and and_4 (and_4_out, A1, B1);
  Hex_Digit_Display hex_digit_display_3 (.value({X3, X2, X1, X0}));  // open: dp
  Adder #(.width(1)) adder_1 (.a(and_2_out), .b(and_3_out), .out(X1), .cin(1'b0), .cout(adder_1_cout));
  Adder #(.width(1)) adder_2 (.a(adder_1_cout), .b(and_4_out), .out(X2), .cin(1'b0), .cout(X3));
endmodule
