// Logisim project Q1.circ as structural Verilog: 2 circuits, main circuit D FF
module D_FF (
  input  Preset,
  input  D,
  input  Clock,
  input  E,
  input  Clear,
  output Q,
  output Q_BAR
);

  wire nand_1_out, nand_2_out, nand_3_out, nand_4_out, nand_5_out, nand_6_out, not_1_out, not_2_out,
       not_3_out, not_4_out;

  not not_1 (not_1_out, Preset);
  not not_2 (not_2_out, D);
  not not_3 (not_3_out, Clear);
  nand nand_1 (nand_1_out, D, E, Clock);
  nand nand_2 (nand_2_out, Clock, E, not_2_out);
  nand nand_3 (nand_3_out, not_1_out, nand_1_out, nand_4_out);
  nand nand_4 (nand_4_out, nand_3_out, nand_2_out, not_3_out);
  not not_4 (not_4_out, Clock);
  nand nand_5 (nand_5_out, nand_3_out, not_4_out);
  nand nand_6 (nand_6_out, not_4_out, nand_4_out);
  nand nand_7 (Q, not_1_out, nand_5_out, Q_BAR);
  nand nand_8 (Q_BAR, Q, nand_6_out, not_3_out);
endmodule

module _4bit_SISO (
  input  in_1,
  input  Serial_Input,
  input  E,
  input  Clear,
  output out_5
);

  wire Clock_out, d_ff_1_q, d_ff_2_q, d_ff_3_q;

  D_FF d_ff_1 (.Preset(in_1), .D(Serial_Input), .E(E), .Clear(Clear), .Q(d_ff_1_q), .Clock(Clock_out));  // open: Q_BAR
  Clock Clock (.out(Clock_out));
  D_FF d_ff_2 (.Preset(in_1), .D(d_ff_1_q), .E(E), .Clear(Clear), .Q(d_ff_2_q), .Clock(Clock_out));  // open: Q_BAR
  D_FF d_ff_3 (.Preset(in_1), .D(d_ff_2_q), .E(E), .Clear(Clear), .Q(d_ff_3_q), .Clock(Clock_out));  // open: Q_BAR
  D_FF d_ff_4 (.Preset(in_1), .D(d_ff_3_q), .E(E), .Clear(Clear), .Q(out_5), .Clock(Clock_out));  // open: Q_BAR
endmodule
