// Logisim project Q3.circ as structural Verilog: 4 circuits, main circuit MOD 6 COUNTER
module MOD_6_COUNTER (
  input  Clock_In,
  input  E,
  input  Reset,
  output QA,
  output QB,
  output QC,
  output Clock_Out
);

  wire and_1_out, d_ff_1_qn, d_ff_2_qn, d_ff_3_qn;

  D_Flip_Flop d_ff_1 (
    .clk(Clock_In), .D(d_ff_1_qn), .Q(QA), .Qn(d_ff_1_qn), .en(E), .reset(Clock_Out));  // open: preset
  D_Flip_Flop d_ff_2 (
    .clk(d_ff_1_qn), .D(d_ff_2_qn), .Q(QB), .Qn(d_ff_2_qn), .en(E), .reset(Clock_Out));  // open: preset
  or or_1 (Clock_Out, and_1_out, Reset);
  D_Flip_Flop d_ff_3 (
    .clk(d_ff_2_qn), .D(d_ff_3_qn), .Q(QC), .Qn(d_ff_3_qn), .en(E), .reset(Clock_Out));  // open: preset
  and and_1 (and_1_out, QB, QC);
  Hex_Digit_Display hex_digit_display_1 (.value({1'b0, QC, QB, QA}));  // open: dp
endmodule

module MOD_3_COUNTER (
  input  E,
  input  Reset,
  output QA,
  output QB,
  output Clock_Out
);

  wire and_1_out, Clock_In_out, d_ff_1_qn, d_ff_2_qn;

  Clock Clock_In (.out(Clock_In_out));
  D_Flip_Flop d_ff_1 (
    .clk(Clock_In_out), .D(d_ff_1_qn), .Q(QA), .Qn(d_ff_1_qn), .en(E), .reset(Clock_Out));  // open: preset
  D_Flip_Flop d_ff_2 (
    .clk(d_ff_1_qn), .D(d_ff_2_qn), .Q(QB), .Qn(d_ff_2_qn), .en(E), .reset(Clock_Out));  // open: preset
  or or_1 (Clock_Out, and_1_out, Reset);
  and and_1 (and_1_out, QB, QA);
  Hex_Digit_Display hex_digit_display_1 (.value({2'b00, QB, QA}));  // open: dp
endmodule

module MOD_10_COUNTER (
  input  E,
  input  Reset,
  output QA,
  output QB,
  output QC,
  output QD,
  output Clock_Out
);

  wire and_1_out, Clock_In_out, d_ff_1_qn, d_ff_2_qn, d_ff_3_qn, d_ff_4_qn;

  Clock Clock_In (.out(Clock_In_out));
  D_Flip_Flop d_ff_1 (
    .clk(Clock_In_out), .D(d_ff_1_qn), .Q(QA), .Qn(d_ff_1_qn), .en(E), .reset(Clock_Out));  // open: preset
  D_Flip_Flop d_ff_2 (
    .clk(d_ff_1_qn), .D(d_ff_2_qn), .Q(QB), .Qn(d_ff_2_qn), .en(E), .reset(Clock_Out));  // open: preset
  or or_1 (Clock_Out, and_1_out, Reset);
  D_Flip_Flop d_ff_3 (
    .clk(d_ff_2_qn), .D(d_ff_3_qn), .Q(QC), .Qn(d_ff_3_qn), .en(E), .reset(Clock_Out));  // open: preset
  and and_1 (and_1_out, QD, QB);
  D_Flip_Flop d_ff_4 (
    .clk(d_ff_3_qn), .D(d_ff_4_qn), .Q(QD), .Qn(d_ff_4_qn), .en(E), .reset(Clock_Out));  // open: preset
  Hex_Digit_Display hex_digit_display_1 (.value({QD, QC, QB, QA}));  // open: dp
endmodule

module Digital_Clock (
);

  MOD_3_COUNTER mod_3_counter_1 ();  // open: E, Clock_Out, QA, QB, Reset
endmodule
