// Logisim project q1.circ as structural Verilog: 2 circuits, main circuit Adder and Logic Circuit
module Adder_and_Logic_Circuit (
  input  [7:0] AC,
  input  [7:0] DR,
  input  [7:0] INPR,
  input  [2:0] in_4,
  output [7:0] out_5
);

  wire [7:0] adder_1_out, adder_2_out, and_1_out, shifter_1_out, shifter_2_out, xor_1_out;

  assign and_1_out = AC & DR;  // AND_Gate and_1, 8 bits wide
  Adder adder_1 (.a(AC), .b(DR), .out(adder_1_out), .cin(1'b0));  // open: cout
  assign xor_1_out = AC ^ 8'h1;  // XOR_Gate xor_1, 8 bits wide
  Shifter #(.shift("lr")) shifter_1 (.in(AC), .\dist (3'b001), .out(shifter_1_out));
  Shifter shifter_2 (.in(AC), .\dist (3'b001), .out(shifter_2_out));
  Adder adder_2 (.a(8'h1), .b(AC), .out(adder_2_out), .cin(1'b0));  // open: cout
  Multiplexer #(.select(3), .width(8)) multiplexer_1 (
    .in0(and_1_out), .in1(adder_1_out), .in2(DR), .in3(INPR), .in4(xor_1_out), .in5(shifter_1_out),
    .in6(shifter_2_out), .in7(adder_2_out), .out(out_5), .sel(in_4));  // open: en
endmodule

module Accumulator (
  input  [7:0] DR,
  input  [7:0] INPR,
  input  Load,
  input  Clear,
  input  [2:0] Select_Line,
  output [7:0] AC
);

  wire Clock_out;
  wire [7:0] adder_and_logic_circuit_1_out_5;

  Adder_and_Logic_Circuit adder_and_logic_circuit_1 (
    .AC(AC), .DR(DR), .INPR(INPR), .in_4(Select_Line), .out_5(adder_and_logic_circuit_1_out_5));
  Clock Clock (.out(Clock_out));
  Register register_1 (.D(adder_and_logic_circuit_1_out_5), .en(Load), .Q(AC), .clk(Clock_out), .clr(Clear));
endmodule
