// Logisim project q2.circ as structural Verilog: 2 circuits, main circuit ALU-8BIT
module ALU_8BIT (
  input  S1,
  input  S0,
  input  CIN,
  input  [7:0] A,
  input  [7:0] B,
  output [7:0] F
);

  wire [7:0] adder_1_out, and_1_out, multiplexer_1_out, multiplexer_2_out, multiplexer_3_out,
       multiplexer_4_out, not_1_out, shifter_1_out, shifter_2_out, xor_1_out;

  assign not_1_out = ~B;  // NOT_Gate not_1, 8 bits wide
  assign xor_1_out = A ^ B;  // XOR_Gate xor_1, 8 bits wide
  assign and_1_out = A & B;  // AND_Gate and_1, 8 bits wide
  Shifter #(.shift("rl")) shifter_1 (.in(A), .\dist (3'b001), .out(shifter_1_out));
  Shifter #(.shift("ar")) shifter_2 (.in(B), .\dist (3'b001), .out(shifter_2_out));
  Multiplexer #(.select(2), .width(8)) multiplexer_1 (
    .in0({8{1'b0}}), .in1(not_1_out), .in2(B), .in3(8'hfe), .out(multiplexer_1_out), .sel({S0, CIN}));  // open: en
  Multiplexer #(.width(8)) multiplexer_2 (
    .in0(xor_1_out), .in1(and_1_out), .out(multiplexer_2_out), .sel(CIN));  // open: en
  Multiplexer #(.width(8)) multiplexer_3 (
    .in0(shifter_1_out), .in1(shifter_2_out), .out(multiplexer_3_out), .sel(CIN));  // open: en
  Adder adder_1 (.a(multiplexer_1_out), .b(A), .out(adder_1_out), .cin(CIN));  // open: cout
  Multiplexer #(.width(8)) multiplexer_4 (
    .in0(multiplexer_2_out), .in1(multiplexer_3_out), .out(multiplexer_4_out), .sel(S0));  // open: en
  Multiplexer #(.width(8)) multiplexer_5 (.in0(adder_1_out), .in1(multiplexer_4_out), .out(F), .sel(S1));  // open: en
endmodule

module CPU (
  input  [7:0] INPUT,
  input  [2:0] SEL_D,
  input  [2:0] SEL_A,
  input  [2:0] SEL_B,
  input  [2:0] OPR
);

  wire clock_1_out, decoder_1_out1, decoder_1_out2, decoder_1_out3, decoder_1_out4, decoder_1_out5,
       decoder_1_out6, decoder_1_out7;
  wire [7:0] ALU_8_BIT_f, multiplexer_1_out, multiplexer_2_out, register_1_q, register_2_q, register_3_q,
       register_4_q, register_5_q, register_6_q, register_7_q;

  Decoder #(.select(3), .enable("false")) decoder_1 (
    .out1(decoder_1_out1), .out2(decoder_1_out2), .out3(decoder_1_out3), .out4(decoder_1_out4),
    .out5(decoder_1_out5), .out6(decoder_1_out6), .out7(decoder_1_out7), .sel(SEL_D));  // open: out0
  Clock clock_1 (.out(clock_1_out));
  Register register_1 (.D(ALU_8_BIT_f), .en(decoder_1_out1), .Q(register_1_q), .clk(clock_1_out));  // open: clr
  Register register_2 (.D(ALU_8_BIT_f), .en(decoder_1_out2), .Q(register_2_q), .clk(clock_1_out));  // open: clr
  Register register_3 (.D(ALU_8_BIT_f), .en(decoder_1_out3), .Q(register_3_q), .clk(clock_1_out));  // open: clr
  Register register_4 (.D(ALU_8_BIT_f), .en(decoder_1_out4), .Q(register_4_q), .clk(clock_1_out));  // open: clr
  Register register_5 (.D(ALU_8_BIT_f), .en(decoder_1_out5), .Q(register_5_q), .clk(clock_1_out));  // open: clr
  Register register_6 (.D(ALU_8_BIT_f), .en(decoder_1_out6), .Q(register_6_q), .clk(clock_1_out));  // open: clr
  Register register_7 (.D(ALU_8_BIT_f), .en(decoder_1_out7), .Q(register_7_q), .clk(clock_1_out));  // open: clr
  Multiplexer #(.select(3), .width(8), .enable("false")) multiplexer_1 (
    .in0(INPUT), .in1(register_1_q), .in2(register_2_q), .in3(register_3_q), .in4(register_4_q),
    .in5(register_5_q), .in6(register_6_q), .in7(register_7_q), .out(multiplexer_1_out), .sel(SEL_A));
  Multiplexer #(.select(3), .width(8), .enable("false")) multiplexer_2 (
    .in0(INPUT), .in1(register_1_q), .in2(register_2_q), .in3(register_3_q), .in4(register_4_q),
    .in5(register_5_q), .in6(register_6_q), .in7(register_7_q), .out(multiplexer_2_out), .sel(SEL_B));
  ALU_8BIT ALU_8_BIT (
    .A(multiplexer_1_out), .F(ALU_8_BIT_f), .B(multiplexer_2_out), .S1(OPR[2]), .S0(OPR[1]), .CIN(OPR[0]));
endmodule
