// Logisim project Q3.circ as structural Verilog: 4 circuits, main circuit MOD 6 COUNTER
// MOD 6
module MOD_6_COUNTER (
  input  Clock_In,
  input  E,
  input  Reset,
  output QA,
  output QB,
  output QC,
  output Clock_Out
);

  wire and_1_out, d_ff_1_qn, d_ff_2_qn, d_ff_3_qn;

  D_Flip_Flop d_ff_1 (
    .clk(Clock_In), .D(d_ff_1_qn), .Q(QA), .Qn(d_ff_1_qn), .en(E), .reset(Clock_Out));  // open: preset
  D_Flip_Flop d_ff_2 (
    .clk(d_ff_1_qn), .D(d_ff_2_qn), .Q(QB), .Qn(d_ff_2_qn), .en(E), .reset(Clock_Out));  // open: preset
  or or_1 (Clock_Out, and_1_out, Reset);
  D_Flip_Flop d_ff_3 (
    .clk(d_ff_2_qn), .D(d_ff_3_qn), .Q(QC), .Qn(d_ff_3_qn), .en(E), .reset(Clock_Out));  // open: preset
  and and_1 (and_1_out, QB, QC);
  Hex_Digit_Display hex_digit_display_1 (.value({1'b0, QC, QB, QA}));  // open: dp
endmodule

// MOD 3
module MOD_3_COUNTER (
  input  Clock_In,
  input  E,
  input  Reset,
  output QA,
  output QB,
  output Clock_Out
);

  wire and_1_out, d_ff_1_qn, d_ff_2_qn;

  D_Flip_Flop d_ff_1 (
    .clk(Clock_In), .D(d_ff_1_qn), .Q(QA), .Qn(d_ff_1_qn), .en(E), .reset(Clock_Out));  // open: preset
  D_Flip_Flop d_ff_2 (
    .clk(d_ff_1_qn), .D(d_ff_2_qn), .Q(QB), .Qn(d_ff_2_qn), .en(E), .reset(Clock_Out));  // open: preset
  or or_1 (Clock_Out, and_1_out, Reset);
  and and_1 (and_1_out, QB, QA);
  Hex_Digit_Display hex_digit_display_1 (.value({2'b00, QB, QA}));  // open: dp
endmodule

// MOD 10
module MOD_10_COUNTER (
  input  Clock_In,
  input  E,
  input  Reset,
  output QA,
  output QB,
  output QC,
  output QD,
  output Clock_Out
);

  wire and_1_out, d_ff_1_qn, d_ff_2_qn, d_ff_3_qn, d_ff_4_qn;

  D_Flip_Flop d_ff_1 (
    .clk(Clock_In), .D(d_ff_1_qn), .Q(QA), .Qn(d_ff_1_qn), .en(E), .reset(Clock_Out));  // open: preset
  D_Flip_Flop d_ff_2 (
    .clk(d_ff_1_qn), .D(d_ff_2_qn), .Q(QB), .Qn(d_ff_2_qn), .en(E), .reset(Clock_Out));  // open: preset
  or or_1 (Clock_Out, and_1_out, Reset);
  D_Flip_Flop d_ff_3 (
    .clk(d_ff_2_qn), .D(d_ff_3_qn), .Q(QC), .Qn(d_ff_3_qn), .en(E), .reset(Clock_Out));  // open: preset
  and and_1 (and_1_out, QD, QB);
  D_Flip_Flop d_ff_4 (
    .clk(d_ff_3_qn), .D(d_ff_4_qn), .Q(QD), .Qn(d_ff_4_qn), .en(E), .reset(Clock_Out));  // open: preset
  Hex_Digit_Display hex_digit_display_1 (.value({QD, QC, QB, QA}));  // open: dp
endmodule

module Digital_Clock (
  input  Enable,
  input  Reset_prime,
  input  _24_12
);

  wire and_1_out, and_2_out, clock_1_out, mod_6_counter_1_clock_out, mod_6_counter_2_clock_out,
       mod_10_counter_1_clock_out, mod_10_counter_2_clock_out, mod_10_counter_3_clock_out, or_1_out, or_2_out;
  wire [1:0] mod_3_counter_1_qa;
  wire [2:0] mod_6_counter_1_qa, mod_6_counter_2_qa;
  wire [3:0] mod_10_counter_1_qa, mod_10_counter_2_qa, mod_10_counter_3_qa;

  Hex_Digit_Display hex_digit_display_1 (.value({2'b00, mod_3_counter_1_qa}));  // open: dp
  MOD_3_COUNTER mod_3_counter_1 (
    .E(Enable), .QA(mod_3_counter_1_qa[0]), .QB(mod_3_counter_1_qa[1]), .Reset(or_2_out),
    .Clock_In(mod_10_counter_1_clock_out));  // open: Clock_Out
  Hex_Digit_Display hex_digit_display_2 (.value(mod_10_counter_1_qa));  // open: dp
  MOD_10_COUNTER mod_10_counter_1 (
    .E(Enable), .Clock_Out(mod_10_counter_1_clock_out), .QA(mod_10_counter_1_qa[0]),
    .QB(mod_10_counter_1_qa[1]), .QC(mod_10_counter_1_qa[2]), .QD(mod_10_counter_1_qa[3]), .Reset(or_2_out),
    .Clock_In(mod_6_counter_1_clock_out));
  Hex_Digit_Display hex_digit_display_3 (.value({1'b0, mod_6_counter_1_qa}));  // open: dp
  MOD_6_COUNTER mod_6_counter_1 (
    .E(Enable), .Clock_Out(mod_6_counter_1_clock_out), .QA(mod_6_counter_1_qa[0]),
    .QB(mod_6_counter_1_qa[1]), .QC(mod_6_counter_1_qa[2]), .Reset(or_2_out),
    .Clock_In(mod_10_counter_2_clock_out));
  MOD_10_COUNTER mod_10_counter_2 (
    .E(Enable), .Clock_Out(mod_10_counter_2_clock_out), .QA(mod_10_counter_2_qa[0]),
    .QB(mod_10_counter_2_qa[1]), .QC(mod_10_counter_2_qa[2]), .QD(mod_10_counter_2_qa[3]), .Reset(or_2_out),
    .Clock_In(mod_6_counter_2_clock_out));
  and and_1 (and_1_out, mod_10_counter_1_qa[2], ~_24_12, mod_3_counter_1_qa[1]);  // AND_Gate
  or or_1 (or_1_out, and_1_out, and_2_out);
  and and_2 (and_2_out, mod_10_counter_1_qa[1], _24_12, mod_3_counter_1_qa[0]);
  Hex_Digit_Display hex_digit_display_4 (.value(mod_10_counter_2_qa));  // open: dp
  or or_2 (or_2_out, or_1_out, Reset_prime);
  Hex_Digit_Display hex_digit_display_5 (.value({1'b0, mod_6_counter_2_qa}));  // open: dp
  MOD_6_COUNTER mod_6_counter_2 (
    .E(Enable), .Clock_Out(mod_6_counter_2_clock_out), .QA(mod_6_counter_2_qa[0]),
    .QB(mod_6_counter_2_qa[1]), .QC(mod_6_counter_2_qa[2]), .Reset(or_2_out),
    .Clock_In(mod_10_counter_3_clock_out));
  Hex_Digit_Display hex_digit_display_6 (.value(mod_10_counter_3_qa));  // open: dp
  MOD_10_COUNTER mod_10_counter_3 (
    .E(Enable), .Clock_Out(mod_10_counter_3_clock_out), .QA(mod_10_counter_3_qa[0]),
    .QB(mod_10_counter_3_qa[1]), .QC(mod_10_counter_3_qa[2]), .QD(mod_10_counter_3_qa[3]), .Reset(or_2_out),
    .Clock_In(clock_1_out));
  Clock clock_1 (.out(clock_1_out));

  // Notes on the sheet:
  //   Hours
  //   1- 12 and 0-24 format
  //   Minutes
  //   Digital Clock System
  //   Seconds
endmodule
