// Logisim project ex9.circ as structural Verilog: 4 circuits, main circuit 8*8 ROM
module _8_8_ROM (
  input  Clock,
  input  Chip_Select,
  input  [2:0] Address_Line,
  output [7:0] out_4
);

  wire decoder_1_out0, decoder_1_out1, decoder_1_out2, decoder_1_out3, decoder_1_out4, decoder_1_out5,
       decoder_1_out6, decoder_1_out7;
  wire [7:0] register_1_q, register_2_q, register_3_q, register_4_q, register_5_q, register_6_q,
       register_7_q, register_8_q;

  Decoder #(.select(3)) decoder_1 (
    .out0(decoder_1_out0), .out1(decoder_1_out1), .out2(decoder_1_out2), .out3(decoder_1_out3),
    .out4(decoder_1_out4), .out5(decoder_1_out5), .out6(decoder_1_out6), .out7(decoder_1_out7),
    .sel(Address_Line), .en(Chip_Select));
  Register register_1 (.D(8'h2), .en(decoder_1_out0), .Q(register_1_q), .clk(Clock));  // open: clr
  Register register_2 (.D(8'h2), .en(decoder_1_out1), .Q(register_2_q), .clk(Clock));  // open: clr
  Register register_3 (.D(8'h2), .en(decoder_1_out2), .Q(register_3_q), .clk(Clock));  // open: clr
  Register register_4 (.D(8'h2), .en(decoder_1_out3), .Q(register_4_q), .clk(Clock));  // open: clr
  Register register_5 (.D(8'h2), .en(decoder_1_out4), .Q(register_5_q), .clk(Clock));  // open: clr
  Register register_6 (.D(8'h2), .en(decoder_1_out5), .Q(register_6_q), .clk(Clock));  // open: clr
  Register register_7 (.D(8'h2), .en(decoder_1_out6), .Q(register_7_q), .clk(Clock));  // open: clr
  Register register_8 (.D(8'h2), .en(decoder_1_out7), .Q(register_8_q), .clk(Clock));  // open: clr
  Multiplexer #(.select(3), .width(8)) multiplexer_1 (
    .in0(register_1_q), .in1(register_2_q), .in2(register_3_q), .in3(register_4_q), .in4(register_5_q),
    .in5(register_6_q), .in6(register_7_q), .in7(register_8_q), .out(out_4), .sel(Address_Line),
    .en(Chip_Select));
endmodule

module _16_8_RAM (
  input  Write_nRead,
  input  [7:0] Data_In,
  input  Clock,
  input  Clear,
  input  [3:0] Address_Line,
  input  Chip_Select,
  output [7:0] Data_Out
);

  wire decoder_1_out0, decoder_1_out1, decoder_1_out2, decoder_1_out3, decoder_1_out4, decoder_1_out5,
       decoder_1_out6, decoder_1_out7, decoder_1_out8, decoder_1_out9, decoder_1_out10, decoder_1_out11,
       decoder_1_out12, decoder_1_out13, decoder_1_out14, decoder_1_out15, not_1_out;
  wire [7:0] controlled_buffer_1_out, controlled_buffer_2_out, controlled_buffer_3_out,
       controlled_buffer_4_out, controlled_buffer_5_out, controlled_buffer_6_out, controlled_buffer_7_out,
       controlled_buffer_8_out, controlled_buffer_9_out, controlled_buffer_10_out, controlled_buffer_11_out,
       controlled_buffer_12_out, controlled_buffer_13_out, controlled_buffer_14_out,
       controlled_buffer_15_out, controlled_buffer_16_out, controlled_buffer_17_out, register_1_q,
       register_2_q, register_3_q, register_4_q, register_5_q, register_6_q, register_7_q, register_8_q,
       register_9_q, register_10_q, register_11_q, register_12_q, register_13_q, register_14_q,
       register_15_q, register_16_q;

  Decoder #(.select(4)) decoder_1 (
    .out0(decoder_1_out0), .out1(decoder_1_out1), .out2(decoder_1_out2), .out3(decoder_1_out3),
    .out4(decoder_1_out4), .out5(decoder_1_out5), .out6(decoder_1_out6), .out7(decoder_1_out7),
    .out8(decoder_1_out8), .out9(decoder_1_out9), .out10(decoder_1_out10), .out11(decoder_1_out11),
    .out12(decoder_1_out12), .out13(decoder_1_out13), .out14(decoder_1_out14), .out15(decoder_1_out15),
    .sel(Address_Line), .en(Chip_Select));
  assign controlled_buffer_1_out = Write_nRead ? Data_In : 8'bz;  // Controlled_Buffer controlled_buffer_1
  not not_1 (not_1_out, Write_nRead);
  Register register_1 (.D(controlled_buffer_1_out), .en(decoder_1_out0), .Q(register_1_q), .clk(Clock), .clr(Clear));
  Register register_2 (.D(controlled_buffer_1_out), .en(decoder_1_out1), .Q(register_2_q), .clk(Clock), .clr(Clear));
  Register register_3 (.D(controlled_buffer_1_out), .en(decoder_1_out2), .Q(register_3_q), .clk(Clock), .clr(Clear));
  Register register_4 (.D(controlled_buffer_1_out), .en(decoder_1_out3), .Q(register_4_q), .clk(Clock), .clr(Clear));
  Register register_5 (.D(controlled_buffer_1_out), .en(decoder_1_out4), .Q(register_5_q), .clk(Clock), .clr(Clear));
  Register register_6 (.D(controlled_buffer_1_out), .en(decoder_1_out5), .Q(register_6_q), .clk(Clock), .clr(Clear));
  Register register_7 (.D(controlled_buffer_1_out), .en(decoder_1_out6), .Q(register_7_q), .clk(Clock), .clr(Clear));
  Register register_8 (.D(controlled_buffer_1_out), .en(decoder_1_out7), .Q(register_8_q), .clk(Clock), .clr(Clear));
  Register register_9 (.D(controlled_buffer_1_out), .en(decoder_1_out8), .Q(register_9_q), .clk(Clock), .clr(Clear));
  Register register_10 (.D(controlled_buffer_1_out), .en(decoder_1_out9), .Q(register_10_q), .clk(Clock), .clr(Clear));
  Register register_11 (.D(controlled_buffer_1_out), .en(decoder_1_out10), .Q(register_11_q), .clk(Clock), .clr(Clear));
  Register register_12 (.D(controlled_buffer_1_out), .en(decoder_1_out11), .Q(register_12_q), .clk(Clock), .clr(Clear));
  Register register_13 (.D(controlled_buffer_1_out), .en(decoder_1_out12), .Q(register_13_q), .clk(Clock), .clr(Clear));
  Register register_14 (.D(controlled_buffer_1_out), .en(decoder_1_out13), .Q(register_14_q), .clk(Clock), .clr(Clear));
  Register register_15 (.D(controlled_buffer_1_out), .en(decoder_1_out14), .Q(register_15_q), .clk(Clock), .clr(Clear));
  Register register_16 (.D(controlled_buffer_1_out), .en(decoder_1_out15), .Q(register_16_q), .clk(Clock), .clr(Clear));
  assign controlled_buffer_2_out = not_1_out ? register_1_q : 8'bz;  // Controlled_Buffer controlled_buffer_2
  assign controlled_buffer_3_out = not_1_out ? register_2_q : 8'bz;  // Controlled_Buffer controlled_buffer_3
  assign controlled_buffer_4_out = not_1_out ? register_3_q : 8'bz;  // Controlled_Buffer controlled_buffer_4
  assign controlled_buffer_5_out = not_1_out ? register_4_q : 8'bz;  // Controlled_Buffer controlled_buffer_5
  assign controlled_buffer_6_out = not_1_out ? register_5_q : 8'bz;  // Controlled_Buffer controlled_buffer_6
  assign controlled_buffer_7_out = not_1_out ? register_6_q : 8'bz;  // Controlled_Buffer controlled_buffer_7
  assign controlled_buffer_8_out = not_1_out ? register_7_q : 8'bz;  // Controlled_Buffer controlled_buffer_8
  assign controlled_buffer_9_out = not_1_out ? register_8_q : 8'bz;  // Controlled_Buffer controlled_buffer_9
  assign controlled_buffer_10_out = not_1_out ? register_9_q : 8'bz;  // Controlled_Buffer controlled_buffer_10
  assign controlled_buffer_11_out = not_1_out ? register_10_q : 8'bz;  // Controlled_Buffer controlled_buffer_11
  assign controlled_buffer_12_out = not_1_out ? register_11_q : 8'bz;  // Controlled_Buffer controlled_buffer_12
  assign controlled_buffer_13_out = not_1_out ? register_12_q : 8'bz;  // Controlled_Buffer controlled_buffer_13
  assign controlled_buffer_14_out = not_1_out ? register_13_q : 8'bz;  // Controlled_Buffer controlled_buffer_14
  assign controlled_buffer_15_out = not_1_out ? register_14_q : 8'bz;  // Controlled_Buffer controlled_buffer_15
  assign controlled_buffer_16_out = not_1_out ? register_15_q : 8'bz;  // Controlled_Buffer controlled_buffer_16
  assign controlled_buffer_17_out = not_1_out ? register_16_q : 8'bz;  // Controlled_Buffer controlled_buffer_17
  Multiplexer #(.select(4), .width(8)) multiplexer_1 (
    .in0(controlled_buffer_2_out), .in1(controlled_buffer_3_out), .in2(controlled_buffer_4_out),
    .in3(controlled_buffer_5_out), .in4(controlled_buffer_6_out), .in5(controlled_buffer_7_out),
    .in6(controlled_buffer_8_out), .in7(controlled_buffer_9_out), .in8(controlled_buffer_10_out),
    .in9(controlled_buffer_11_out), .in10(controlled_buffer_12_out), .in11(controlled_buffer_13_out),
    .in12(controlled_buffer_14_out), .in13(controlled_buffer_15_out), .in14(controlled_buffer_16_out),
    .in15(controlled_buffer_17_out), .out(Data_Out), .sel(Address_Line), .en(Chip_Select));
endmodule

module _56_8_memeory_system (
  input  [7:0] INPUT,
  input  [3:0] Address_Line,
  input  Write_nRead,
  input  Reset,
  input  [1:0] in_5,
  output [7:0] out_6
);

  wire Clock_out, decoder_1_out0, decoder_1_out1, decoder_1_out2, decoder_1_out3;

  Clock Clock (.out(Clock_out));
  Decoder #(.select(2)) decoder_1 (
    .out0(decoder_1_out0), .out1(decoder_1_out1), .out2(decoder_1_out2), .out3(decoder_1_out3), .sel(in_5));  // open: en
  _16_8_RAM u_16_8_ram_1 (
    .Data_In(INPUT), .Data_Out(out_6), .Write_nRead(Write_nRead), .Chip_Select(decoder_1_out0),
    .Clear(Reset), .Clock(Clock_out), .Address_Line(Address_Line));
  _16_8_RAM u_16_8_ram_2 (
    .Data_In(INPUT), .Data_Out(out_6), .Write_nRead(Write_nRead), .Chip_Select(decoder_1_out1),
    .Clear(Reset), .Clock(Clock_out), .Address_Line(Address_Line));
  _16_8_RAM u_16_8_ram_3 (
    .Data_In(INPUT), .Data_Out(out_6), .Write_nRead(Write_nRead), .Chip_Select(decoder_1_out2),
    .Clear(Reset), .Clock(Clock_out), .Address_Line(Address_Line));
  _8_8_ROM u_8_8_rom_1 (
    .out_4(out_6), .Chip_Select(decoder_1_out3), .Address_Line(Address_Line[2:0]), .Clock(Clock_out));
endmodule

module _384_8_memory_system (
);

  Counter counter_1 ();  // open: load, D, count, Q, carry, clk, clr
  RAM ram_1 ();  // open: addr, data, sel, clk, ld, clr
  ROM #(.addrWidth(7)) rom_1 ();  // open: addr, data, sel
endmodule
